// Logisim project exp_1.circ as structural Verilog: 14 circuits, main circuit exp111
module exp111 (
  input  in_1,
  input  in_2,
  input  in_3,
  output out_4
);

  wire and_1_out, and_2_out, and_3_out;

  and and_1 (and_1_out, in_3, in_1);
  and and_2 (and_2_out, in_2, in_1);
  and and_3 (and_3_out, in_2, in_3);
  or or_1 (out_4, and_1_out, and_2_out, and_3_out);

  // Notes on the sheet:
  //   1. Use basic logic gate to build a 3-input majority voting judger
endmodule

module exp112 (
  input  in_1,
  input  in_2,
  output out_3,
  output out_4
);

  wire transistor_1_out, transistor_2_out;

  Transistor transistor_1 (.in(1'b1), .out(transistor_1_out), .gate(in_1));
  Transistor transistor_2 (.in(transistor_1_out), .out(transistor_2_out), .gate(in_2));
  Transistor #(.\type ("n")) transistor_3 (.in(1'b0), .out(transistor_2_out), .gate(in_2));
  Transistor #(.\type ("n")) transistor_4 (.in(1'b0), .out(transistor_2_out), .gate(in_1));
  or or_1 (out_4, in_1, in_2);
  Transistor transistor_5 (.in(1'b1), .out(out_3), .gate(transistor_2_out));
  Transistor #(.\type ("n")) transistor_6 (.in(1'b0), .out(out_3), .gate(transistor_2_out));

  // Notes on the sheet:
  //   2. Use CMOS transistor to build a 2-input AND gate
endmodule

module exp113 (
  input  in_1,
  input  in_2,
  input  in_3,
  input  in_4,
  input  in_5,
  input  in_6,
  input  in_7,
  input  in_8,
  output out_9,
  output out_10
);

  wire and_1_out, and_2_out, and_3_out, and_4_out, and_5_out, and_6_out, and_7_out, and_8_out, and_9_out,
       and_10_out, and_11_out, and_12_out, and_13_out, nor_1_out, nor_2_out, nor_3_out, nor_4_out, nor_5_out,
       nor_6_out, nor_7_out, xor_1_out, xor_2_out;

  nor nor_1 (nor_1_out, in_1, in_4, in_6, in_8);
  and and_1 (and_1_out, in_6, in_8);
  nor nor_2 (nor_2_out, in_1, in_4);
  and and_2 (and_2_out, in_4, in_8);
  nor nor_3 (nor_3_out, in_1, in_6);
  and and_3 (and_3_out, in_6, in_4);
  nor nor_4 (nor_4_out, in_8, in_1);
  and and_4 (and_4_out, in_8, in_1);
  nor nor_5 (nor_5_out, in_6, in_4);
  and and_5 (and_5_out, in_6, in_1);
  nor nor_6 (nor_6_out, in_4, in_8);
  and and_6 (and_6_out, in_4, in_1);
  nor nor_7 (nor_7_out, in_8, in_6);
  and and_7 (and_7_out, in_8, in_6, in_4, in_1);
  and and_8 (and_8_out, and_1_out, nor_2_out);
  and and_9 (and_9_out, and_2_out, nor_3_out);
  and and_10 (and_10_out, and_3_out, nor_4_out);
  and and_11 (and_11_out, and_4_out, nor_5_out);
  and and_12 (and_12_out, and_5_out, nor_6_out);
  and and_13 (and_13_out, and_6_out, nor_7_out);
  or or_1 (out_9, nor_1_out, and_8_out, and_9_out, and_10_out, and_11_out, and_12_out, and_13_out, and_7_out);
  xor xor_1 (xor_1_out, in_2, in_3);
  xor xor_2 (xor_2_out, in_5, in_7);
  xnor xnor_1 (out_10, xor_1_out, xor_2_out);

  // Notes on the sheet:
  //   3. Build a 4 digits binary odd or even tester.
  //   Answer from internet
endmodule

module exp114 (
);

  wire [4:0] priority_encoder_1_out, priority_encoder_2_out, priority_encoder_3_out, priority_encoder_4_out,
       priority_encoder_5_out, priority_encoder_6_out, priority_encoder_7_out, priority_encoder_8_out,
       priority_encoder_9_out, priority_encoder_10_out, priority_encoder_11_out, priority_encoder_12_out,
       priority_encoder_13_out, priority_encoder_14_out, priority_encoder_15_out;

  DotMatrix #(.matrixrows(5)) dotmatrix_1 (
    .col0(priority_encoder_1_out), .col1(priority_encoder_2_out), .col2(priority_encoder_3_out),
    .col3(priority_encoder_4_out), .col4(priority_encoder_5_out));
  Priority_Encoder #(.select(5)) priority_encoder_1 (
    .in16(1'b1), .out(priority_encoder_1_out));  // open: in0, in1, in2, in3, in4, in5, in6, in7, in8, in9, in10, in11, in12, in13, in14, in15, in17, in18, in19, in20, in21, in22, in23, in24, in25, in26, in27, in28, in29, in30, in31, gs, en_out, en_in
  Priority_Encoder #(.select(5)) priority_encoder_2 (
    .in8(1'b1), .out(priority_encoder_2_out));  // open: in0, in1, in2, in3, in4, in5, in6, in7, in9, in10, in11, in12, in13, in14, in15, in16, in17, in18, in19, in20, in21, in22, in23, in24, in25, in26, in27, in28, in29, in30, in31, gs, en_out, en_in
  Priority_Encoder #(.select(5)) priority_encoder_3 (
    .in7(1'b1), .out(priority_encoder_3_out));  // open: in0, in1, in2, in3, in4, in5, in6, in8, in9, in10, in11, in12, in13, in14, in15, in16, in17, in18, in19, in20, in21, in22, in23, in24, in25, in26, in27, in28, in29, in30, in31, gs, en_out, en_in
  Priority_Encoder #(.select(5)) priority_encoder_4 (
    .in8(1'b1), .out(priority_encoder_4_out));  // open: in0, in1, in2, in3, in4, in5, in6, in7, in9, in10, in11, in12, in13, in14, in15, in16, in17, in18, in19, in20, in21, in22, in23, in24, in25, in26, in27, in28, in29, in30, in31, gs, en_out, en_in
  Priority_Encoder #(.select(5)) priority_encoder_5 (
    .in16(1'b1), .out(priority_encoder_5_out));  // open: in0, in1, in2, in3, in4, in5, in6, in7, in8, in9, in10, in11, in12, in13, in14, in15, in17, in18, in19, in20, in21, in22, in23, in24, in25, in26, in27, in28, in29, in30, in31, gs, en_out, en_in
  Priority_Encoder #(.select(5)) priority_encoder_6 (
    .in0(1'b1), .out(priority_encoder_6_out));  // open: in1, in2, in3, in4, in5, in6, in7, in8, in9, in10, in11, in12, in13, in14, in15, in16, in17, in18, in19, in20, in21, in22, in23, in24, in25, in26, in27, in28, in29, in30, in31, gs, en_out, en_in
  Priority_Encoder #(.select(5)) priority_encoder_7 (
    .in17(1'b1), .out(priority_encoder_7_out));  // open: in0, in1, in2, in3, in4, in5, in6, in7, in8, in9, in10, in11, in12, in13, in14, in15, in16, in18, in19, in20, in21, in22, in23, in24, in25, in26, in27, in28, in29, in30, in31, gs, en_out, en_in
  Priority_Encoder #(.select(5)) priority_encoder_8 (
    .in31(1'b1), .out(priority_encoder_8_out));  // open: in0, in1, in2, in3, in4, in5, in6, in7, in8, in9, in10, in11, in12, in13, in14, in15, in16, in17, in18, in19, in20, in21, in22, in23, in24, in25, in26, in27, in28, in29, in30, gs, en_out, en_in
  Priority_Encoder #(.select(5)) priority_encoder_9 (
    .in16(1'b1), .out(priority_encoder_9_out));  // open: in0, in1, in2, in3, in4, in5, in6, in7, in8, in9, in10, in11, in12, in13, in14, in15, in17, in18, in19, in20, in21, in22, in23, in24, in25, in26, in27, in28, in29, in30, in31, gs, en_out, en_in
  Priority_Encoder #(.select(5)) priority_encoder_10 (
    .in0(1'b1), .out(priority_encoder_10_out));  // open: in1, in2, in3, in4, in5, in6, in7, in8, in9, in10, in11, in12, in13, in14, in15, in16, in17, in18, in19, in20, in21, in22, in23, in24, in25, in26, in27, in28, in29, in30, in31, gs, en_out, en_in
  DotMatrix #(.matrixrows(5)) dotmatrix_2 (
    .col0(priority_encoder_6_out), .col1(priority_encoder_7_out), .col2(priority_encoder_8_out),
    .col3(priority_encoder_9_out), .col4(priority_encoder_10_out));
  DotMatrix #(.matrixrows(5)) dotmatrix_3 (
    .col0(priority_encoder_11_out), .col1(priority_encoder_12_out), .col2(priority_encoder_13_out),
    .col3(priority_encoder_14_out), .col4(priority_encoder_15_out));
  Priority_Encoder #(.select(5)) priority_encoder_11 (
    .in16(1'b1), .out(priority_encoder_11_out));  // open: in0, in1, in2, in3, in4, in5, in6, in7, in8, in9, in10, in11, in12, in13, in14, in15, in17, in18, in19, in20, in21, in22, in23, in24, in25, in26, in27, in28, in29, in30, in31, gs, en_out, en_in
  Priority_Encoder #(.select(5)) priority_encoder_12 (
    .in8(1'b1), .out(priority_encoder_12_out));  // open: in0, in1, in2, in3, in4, in5, in6, in7, in9, in10, in11, in12, in13, in14, in15, in16, in17, in18, in19, in20, in21, in22, in23, in24, in25, in26, in27, in28, in29, in30, in31, gs, en_out, en_in
  Priority_Encoder #(.select(5)) priority_encoder_13 (
    .in7(1'b1), .out(priority_encoder_13_out));  // open: in0, in1, in2, in3, in4, in5, in6, in8, in9, in10, in11, in12, in13, in14, in15, in16, in17, in18, in19, in20, in21, in22, in23, in24, in25, in26, in27, in28, in29, in30, in31, gs, en_out, en_in
  Priority_Encoder #(.select(5)) priority_encoder_14 (
    .in8(1'b1), .out(priority_encoder_14_out));  // open: in0, in1, in2, in3, in4, in5, in6, in7, in9, in10, in11, in12, in13, in14, in15, in16, in17, in18, in19, in20, in21, in22, in23, in24, in25, in26, in27, in28, in29, in30, in31, gs, en_out, en_in
  Priority_Encoder #(.select(5)) priority_encoder_15 (
    .in16(1'b1), .out(priority_encoder_15_out));  // open: in0, in1, in2, in3, in4, in5, in6, in7, in8, in9, in10, in11, in12, in13, in14, in15, in17, in18, in19, in20, in21, in22, in23, in24, in25, in26, in27, in28, in29, in30, in31, gs, en_out, en_in
endmodule

module exp125 (
  input  A,
  input  B,
  input  C,
  input  in_4,
  input  in_5,
  input  in_6,
  output out_7,
  output out_8,
  output out_9,
  output out_10,
  output out_11,
  output out_12,
  output out_13,
  output out_14
);

  wire and_1_out, not_1_out, not_2_out, not_3_out, not_4_out, not_5_out, not_6_out, not_7_out;

  not not_1 (not_1_out, A);
  not not_2 (not_2_out, B);
  not not_3 (not_3_out, C);
  not not_4 (not_4_out, in_4);
  not not_5 (not_5_out, not_1_out);
  not not_6 (not_6_out, not_2_out);
  not not_7 (not_7_out, not_3_out);
  and and_1 (and_1_out, ~not_4_out, ~in_5, ~in_6);  // AND_Gate
  nand nand_1 (out_7, not_1_out, not_2_out, not_3_out, and_1_out);
  nand nand_2 (out_8, not_2_out, not_3_out, not_5_out, and_1_out);
  nand nand_3 (out_9, not_1_out, not_3_out, not_6_out, and_1_out);
  nand nand_4 (out_10, not_3_out, not_5_out, not_6_out, and_1_out);
  nand nand_5 (out_11, not_7_out, not_1_out, not_2_out, and_1_out);
  nand nand_6 (out_12, not_5_out, not_7_out, not_2_out, and_1_out);
  nand nand_7 (out_13, not_1_out, not_6_out, not_7_out, and_1_out);
  nand nand_8 (out_14, not_5_out, not_6_out, not_7_out, and_1_out);

  // Notes on the sheet:
  //   0
  //   1
  //   2
  //   3
  //   4
  //   5
  //   6
  //   7
endmodule

module exp126 (
  input  in_1,
  input  in_2,
  input  in_3,
  input  in_4,
  input  in_5,
  input  in_6,
  input  [3:0] in_7,
  input  in_8,
  input  in_9,
  input  in_10,
  input  in_11,
  input  in_12,
  input  in_13,
  input  in_14,
  input  in_15,
  input  in_16
);

  wire [3:0] priority_encoder_1_out;

  Hex_Digit_Display hex_digit_display_1 (.value(in_7));  // open: dp
  Priority_Encoder #(.select(4)) priority_encoder_1 (
    .in0(1'b1), .in1(in_1), .in2(in_2), .in3(in_3), .in4(in_4), .in5(in_5), .in6(in_6), .in7(in_8),
    .in8(in_9), .in9(in_10), .in10(in_11), .in11(in_12), .in12(in_13), .in13(in_14), .in14(in_15),
    .in15(in_16), .out(priority_encoder_1_out));  // open: gs, en_out, en_in
  Hex_Digit_Display hex_digit_display_2 (.value(priority_encoder_1_out));  // open: dp
endmodule

module exp127_handmade_mux (
  input  I1,
  input  I2,
  input  [1:0] in_3,
  output out_4
);

  wire and_1_out, and_2_out, not_1_out, not_2_out;

  not not_1 (not_1_out, in_3[1]);
  not not_2 (not_2_out, in_3[0]);
  and and_1 (and_1_out, not_1_out, I2, in_3[0]);
  and and_2 (and_2_out, I1, in_3[1], not_2_out);
  or or_1 (out_4, and_1_out, and_2_out);

  // Notes on the sheet:
  //   Convert one 2 bits to two 1 bits
endmodule

module exp127 (
  input  in_1,
  input  in_2,
  input  in_3,
  input  in_4,
  input  [3:0] in_5,
  output out_6
);

  wire [1:0] exp127_handmade_mux_2_out_4;

  exp127_handmade_mux exp127_handmade_mux_1 (
    .I1(in_1), .I2(in_2), .in_3({in_5[2], in_5[3]}), .out_4(exp127_handmade_mux_2_out_4[1]));
  exp127_handmade_mux exp127_handmade_mux_2 (
    .I1(in_3), .I2(in_4), .in_3(in_5[1:0]), .out_4(exp127_handmade_mux_2_out_4[0]));
  exp127_handmade_mux exp127_handmade_mux_3 (
    .I1(exp127_handmade_mux_2_out_4[1]), .I2(exp127_handmade_mux_2_out_4[0]),
    .in_3(exp127_handmade_mux_2_out_4), .out_4(out_6));
endmodule

module exp128 (
  input  [3:0] in_1,
  input  [3:0] in_2
);

  wire exp128_handmade_fa_1_cout, exp128_handmade_fa_2_cout, exp128_handmade_fa_3_cout;
  wire [0:0] exp128_handmade_fa_4_cout;
  wire [3:0] exp128_handmade_fa_1_f;

  exp128_handmade_fa exp128_handmade_fa_1 (
    .A(in_1[0]), .B(in_2[0]), .Cin(1'b0), .Cout(exp128_handmade_fa_1_cout), .F(exp128_handmade_fa_1_f[0]));
  exp128_handmade_fa exp128_handmade_fa_2 (
    .A(in_1[1]), .B(in_2[1]), .Cin(exp128_handmade_fa_1_cout), .Cout(exp128_handmade_fa_2_cout),
    .F(exp128_handmade_fa_1_f[1]));
  exp128_handmade_fa exp128_handmade_fa_3 (
    .A(in_1[2]), .B(in_2[2]), .Cin(exp128_handmade_fa_2_cout), .Cout(exp128_handmade_fa_3_cout),
    .F(exp128_handmade_fa_1_f[2]));
  exp128_handmade_fa exp128_handmade_fa_4 (
    .A(in_1[3]), .B(in_2[3]), .Cin(exp128_handmade_fa_3_cout), .Cout(exp128_handmade_fa_4_cout[0]),
    .F(exp128_handmade_fa_1_f[3]));
  Hex_Digit_Display hex_digit_display_1 (.value({3'b000, exp128_handmade_fa_4_cout[0]}));  // open: dp
  Hex_Digit_Display #(.decimalPoint("false")) hex_digit_display_2 (.value(exp128_handmade_fa_1_f));
endmodule

module exp128_handmade_fa (
  input  A,
  input  B,
  input  Cin,
  output Cout,
  output F
);

  wire and_1_out, and_2_out, and_3_out;

  and and_1 (and_1_out, A, B);
  and and_2 (and_2_out, A, Cin);
  and and_3 (and_3_out, B, Cin);
  or or_1 (Cout, and_1_out, and_2_out, and_3_out);
  ExactlyOne xor_1 (.out(F), .in0(A), .in1(B), .in2(Cin));
endmodule

module exp139 (
);

  wire clock_1_out, counter_1_carry, d_ff_1_q;
  wire [3:0] counter_1_q, counter_2_q;

  Clock clock_1 (.out(clock_1_out));
  D_Flip_Flop d_ff_1 (.D(counter_1_carry), .clk(clock_1_out), .Q(d_ff_1_q));  // open: Qn, preset, reset
  Counter #(.max('h9), .width(4)) counter_1 (
    .count(1'b1), .Q(counter_1_q), .carry(counter_1_carry), .clk(clock_1_out));  // open: load, D, up, clr
  Counter #(.max('h9), .width(4)) counter_2 (
    .count(1'b1), .Q(counter_2_q), .clk(d_ff_1_q));  // open: load, D, carry, up, clr
  Hex_Digit_Display #(.decimalPoint("false")) hex_digit_display_1 (.value(counter_2_q));
  Hex_Digit_Display #(.decimalPoint("false")) hex_digit_display_2 (.value(counter_1_q));
endmodule

module exp1310_abandoned_register (
  input  [4:0] RW,
  input  [31:0] in_2,
  input  WE,
  input  [4:0] RA,
  input  [4:0] RB,
  output [31:0] out_6,
  output [31:0] out_7
);

  wire and_1_out, and_2_out, and_3_out, and_4_out, and_5_out, and_6_out, and_7_out, and_8_out, and_9_out,
       and_10_out, and_11_out, and_12_out, and_13_out, and_14_out, and_15_out, and_16_out, and_17_out,
       and_18_out, and_19_out, and_20_out, and_21_out, and_22_out, and_23_out, and_24_out, and_25_out,
       and_26_out, and_27_out, and_28_out, and_29_out, and_30_out, and_31_out, and_32_out, clock_1_out,
       d_ff_1_q, d_ff_2_q, d_ff_3_q, d_ff_4_q, d_ff_5_q, d_ff_6_q, d_ff_7_q, d_ff_8_q, d_ff_9_q, d_ff_10_q,
       d_ff_11_q, d_ff_12_q, d_ff_13_q, d_ff_14_q, d_ff_15_q, d_ff_16_q, d_ff_17_q, d_ff_18_q, d_ff_19_q,
       d_ff_20_q, d_ff_21_q, d_ff_22_q, d_ff_23_q, d_ff_24_q, d_ff_25_q, d_ff_26_q, d_ff_27_q, d_ff_28_q,
       d_ff_29_q, d_ff_30_q, d_ff_31_q, d_ff_32_q, decoder_1_out0, decoder_1_out1, decoder_1_out2,
       decoder_1_out3, decoder_1_out4, decoder_1_out5, decoder_1_out6, decoder_1_out7, decoder_1_out8,
       decoder_1_out9, decoder_1_out10, decoder_1_out11, decoder_1_out12, decoder_1_out13, decoder_1_out14,
       decoder_1_out15, decoder_1_out16, decoder_1_out17, decoder_1_out18, decoder_1_out19, decoder_1_out20,
       decoder_1_out21, decoder_1_out22, decoder_1_out23, decoder_1_out24, decoder_1_out25, decoder_1_out26,
       decoder_1_out27, decoder_1_out28, decoder_1_out29, decoder_1_out30, decoder_1_out31,
       multiplexer_1_out, multiplexer_2_out;

  Clock clock_1 (.out(clock_1_out));
  Decoder #(.select(5)) decoder_1 (
    .out0(decoder_1_out0), .out1(decoder_1_out1), .out2(decoder_1_out2), .out3(decoder_1_out3),
    .out4(decoder_1_out4), .out5(decoder_1_out5), .out6(decoder_1_out6), .out7(decoder_1_out7),
    .out8(decoder_1_out8), .out9(decoder_1_out9), .out10(decoder_1_out10), .out11(decoder_1_out11),
    .out12(decoder_1_out12), .out13(decoder_1_out13), .out14(decoder_1_out14), .out15(decoder_1_out15),
    .out16(decoder_1_out16), .out17(decoder_1_out17), .out18(decoder_1_out18), .out19(decoder_1_out19),
    .out20(decoder_1_out20), .out21(decoder_1_out21), .out22(decoder_1_out22), .out23(decoder_1_out23),
    .out24(decoder_1_out24), .out25(decoder_1_out25), .out26(decoder_1_out26), .out27(decoder_1_out27),
    .out28(decoder_1_out28), .out29(decoder_1_out29), .out30(decoder_1_out30), .out31(decoder_1_out31),
    .sel(RW));  // open: en
  D_Flip_Flop d_ff_1 (.D(and_1_out), .clk(clock_1_out), .Q(d_ff_1_q));  // open: Qn, preset, reset
  and and_1 (and_1_out, in_2[0], WE, decoder_1_out0);
  D_Flip_Flop d_ff_2 (.D(and_2_out), .clk(clock_1_out), .Q(d_ff_2_q));  // open: Qn, preset, reset
  and and_2 (and_2_out, in_2[1], WE, decoder_1_out1);
  D_Flip_Flop d_ff_3 (.D(and_3_out), .clk(clock_1_out), .Q(d_ff_3_q));  // open: Qn, preset, reset
  and and_3 (and_3_out, in_2[2], WE, decoder_1_out2);
  D_Flip_Flop d_ff_4 (.D(and_4_out), .clk(clock_1_out), .Q(d_ff_4_q));  // open: Qn, preset, reset
  and and_4 (and_4_out, in_2[3], WE, decoder_1_out3);
  D_Flip_Flop d_ff_5 (.D(and_5_out), .clk(clock_1_out), .Q(d_ff_5_q));  // open: Qn, preset, reset
  and and_5 (and_5_out, in_2[4], WE, decoder_1_out4);
  D_Flip_Flop d_ff_6 (.D(and_6_out), .clk(clock_1_out), .Q(d_ff_6_q));  // open: Qn, preset, reset
  and and_6 (and_6_out, in_2[5], WE, decoder_1_out5);
  D_Flip_Flop d_ff_7 (.D(and_7_out), .clk(clock_1_out), .Q(d_ff_7_q));  // open: Qn, preset, reset
  and and_7 (and_7_out, in_2[6], WE, decoder_1_out6);
  D_Flip_Flop d_ff_8 (.D(and_8_out), .clk(clock_1_out), .Q(d_ff_8_q));  // open: Qn, preset, reset
  and and_8 (and_8_out, in_2[7], WE, decoder_1_out7);
  Multiplexer #(.select(5)) multiplexer_1 (
    .in0(d_ff_1_q), .in1(d_ff_2_q), .in2(d_ff_3_q), .in3(d_ff_4_q), .in4(d_ff_5_q), .in5(d_ff_6_q),
    .in6(d_ff_7_q), .in7(d_ff_8_q), .in8(d_ff_9_q), .in9(d_ff_10_q), .in10(d_ff_11_q), .in11(d_ff_12_q),
    .in12(d_ff_13_q), .in13(d_ff_14_q), .in14(d_ff_15_q), .in15(d_ff_16_q), .in16(d_ff_17_q),
    .in17(d_ff_18_q), .in18(d_ff_19_q), .in19(d_ff_20_q), .in20(d_ff_21_q), .in21(d_ff_22_q),
    .in22(d_ff_23_q), .in23(d_ff_24_q), .in24(d_ff_25_q), .in25(d_ff_26_q), .in26(d_ff_27_q),
    .in27(d_ff_28_q), .in28(d_ff_29_q), .in29(d_ff_30_q), .in30(d_ff_31_q), .in31(d_ff_32_q),
    .out(multiplexer_1_out), .sel(RA));
  Multiplexer #(.select(5)) multiplexer_2 (
    .in0(d_ff_1_q), .in1(d_ff_2_q), .in2(d_ff_3_q), .in3(d_ff_4_q), .in4(d_ff_5_q), .in5(d_ff_6_q),
    .in6(d_ff_7_q), .in7(d_ff_8_q), .in8(d_ff_9_q), .in9(d_ff_10_q), .in10(d_ff_11_q), .in11(d_ff_12_q),
    .in12(d_ff_13_q), .in13(d_ff_14_q), .in14(d_ff_15_q), .in15(d_ff_16_q), .in16(d_ff_17_q),
    .in17(d_ff_18_q), .in18(d_ff_19_q), .in19(d_ff_20_q), .in20(d_ff_21_q), .in21(d_ff_22_q),
    .in22(d_ff_23_q), .in23(d_ff_24_q), .in24(d_ff_25_q), .in25(d_ff_26_q), .in26(d_ff_27_q),
    .in27(d_ff_28_q), .in28(d_ff_29_q), .in29(d_ff_30_q), .in30(d_ff_31_q), .in31(d_ff_32_q),
    .out(multiplexer_2_out), .sel(RB));
  and and_9 (and_9_out, in_2[8], WE, decoder_1_out8);
  and and_10 (and_10_out, in_2[9], WE, decoder_1_out9);
  and and_11 (and_11_out, in_2[10], WE, decoder_1_out10);
  and and_12 (and_12_out, in_2[11], WE, decoder_1_out11);
  and and_13 (and_13_out, in_2[12], WE, decoder_1_out12);
  and and_14 (and_14_out, in_2[13], WE, decoder_1_out13);
  and and_15 (and_15_out, in_2[14], WE, decoder_1_out14);
  and and_16 (and_16_out, in_2[15], WE, decoder_1_out15);
  D_Flip_Flop d_ff_9 (.D(and_9_out), .clk(clock_1_out), .Q(d_ff_9_q));  // open: Qn, preset, reset
  D_Flip_Flop d_ff_10 (.D(and_10_out), .clk(clock_1_out), .Q(d_ff_10_q));  // open: Qn, preset, reset
  D_Flip_Flop d_ff_11 (.D(and_11_out), .clk(clock_1_out), .Q(d_ff_11_q));  // open: Qn, preset, reset
  D_Flip_Flop d_ff_12 (.D(and_12_out), .clk(clock_1_out), .Q(d_ff_12_q));  // open: Qn, preset, reset
  D_Flip_Flop d_ff_13 (.D(and_13_out), .clk(clock_1_out), .Q(d_ff_13_q));  // open: Qn, preset, reset
  D_Flip_Flop d_ff_14 (.D(and_14_out), .clk(clock_1_out), .Q(d_ff_14_q));  // open: Qn, preset, reset
  D_Flip_Flop d_ff_15 (.D(and_15_out), .clk(clock_1_out), .Q(d_ff_15_q));  // open: Qn, preset, reset
  D_Flip_Flop d_ff_16 (.D(and_16_out), .clk(clock_1_out), .Q(d_ff_16_q));  // open: Qn, preset, reset
  D_Flip_Flop d_ff_17 (.D(and_17_out), .clk(clock_1_out), .Q(d_ff_17_q));  // open: Qn, preset, reset
  and and_17 (and_17_out, in_2[16], WE, decoder_1_out16);
  D_Flip_Flop d_ff_18 (.D(and_18_out), .clk(clock_1_out), .Q(d_ff_18_q));  // open: Qn, preset, reset
  and and_18 (and_18_out, in_2[17], WE, decoder_1_out17);
  D_Flip_Flop d_ff_19 (.D(and_19_out), .clk(clock_1_out), .Q(d_ff_19_q));  // open: Qn, preset, reset
  and and_19 (and_19_out, in_2[18], WE, decoder_1_out18);
  D_Flip_Flop d_ff_20 (.D(and_20_out), .clk(clock_1_out), .Q(d_ff_20_q));  // open: Qn, preset, reset
  and and_20 (and_20_out, in_2[19], WE, decoder_1_out19);
  D_Flip_Flop d_ff_21 (.D(and_21_out), .clk(clock_1_out), .Q(d_ff_21_q));  // open: Qn, preset, reset
  and and_21 (and_21_out, in_2[20], WE, decoder_1_out20);
  D_Flip_Flop d_ff_22 (.D(and_22_out), .clk(clock_1_out), .Q(d_ff_22_q));  // open: Qn, preset, reset
  and and_22 (and_22_out, in_2[21], WE, decoder_1_out21);
  D_Flip_Flop d_ff_23 (.D(and_23_out), .clk(clock_1_out), .Q(d_ff_23_q));  // open: Qn, preset, reset
  and and_23 (and_23_out, in_2[22], WE, decoder_1_out22);
  D_Flip_Flop d_ff_24 (.D(and_24_out), .clk(clock_1_out), .Q(d_ff_24_q));  // open: Qn, preset, reset
  and and_24 (and_24_out, in_2[23], WE, decoder_1_out23);
  and and_25 (and_25_out, in_2[24], decoder_1_out24);
  and and_26 (and_26_out, in_2[25], decoder_1_out25);
  and and_27 (and_27_out, in_2[26], decoder_1_out26);
  and and_28 (and_28_out, in_2[27], decoder_1_out27);
  and and_29 (and_29_out, in_2[28], decoder_1_out28);
  and and_30 (and_30_out, in_2[29], decoder_1_out29);
  and and_31 (and_31_out, in_2[30], decoder_1_out30);
  and and_32 (and_32_out, in_2[31], decoder_1_out31);
  D_Flip_Flop d_ff_25 (.D(and_25_out), .Q(d_ff_25_q));  // open: clk, Qn, preset, reset
  D_Flip_Flop d_ff_26 (.D(and_26_out), .Q(d_ff_26_q));  // open: clk, Qn, preset, reset
  D_Flip_Flop d_ff_27 (.D(and_27_out), .Q(d_ff_27_q));  // open: clk, Qn, preset, reset
  D_Flip_Flop d_ff_28 (.D(and_28_out), .Q(d_ff_28_q));  // open: clk, Qn, preset, reset
  D_Flip_Flop d_ff_29 (.D(and_29_out), .Q(d_ff_29_q));  // open: clk, Qn, preset, reset
  D_Flip_Flop d_ff_30 (.D(and_30_out), .Q(d_ff_30_q));  // open: clk, Qn, preset, reset
  D_Flip_Flop d_ff_31 (.D(and_31_out), .Q(d_ff_31_q));  // open: clk, Qn, preset, reset
  D_Flip_Flop d_ff_32 (.D(and_32_out), .Q(d_ff_32_q));  // open: clk, Qn, preset, reset

  // Notes on the sheet:
  //   BUSW
  //   BUSOUTA
  //   BUSOUTB
endmodule

module exp1310_handmade_regfile (
  input  [31:0] in_1,
  input  in_2,
  input  [2:0] in_3,
  input  [2:0] in_4,
  input  [2:0] in_5,
  output [31:0] out_6,
  output [31:0] out_7
);

  wire and_1_out, and_2_out, and_3_out, and_4_out, and_5_out, and_6_out, and_7_out, and_8_out, clock_1_out,
       decoder_1_out0, decoder_1_out1, decoder_1_out2, decoder_1_out3, decoder_1_out4, decoder_1_out5,
       decoder_1_out6, decoder_1_out7;
  wire [31:0] register_1_q, register_2_q, register_3_q, register_4_q, register_5_q, register_6_q,
       register_7_q, register_8_q;

  Clock clock_1 (.out(clock_1_out));
  Multiplexer #(.select(3), .width(32)) multiplexer_1 (
    .in0(register_1_q), .in1(register_2_q), .in2(register_3_q), .in3(register_4_q), .in4(register_5_q),
    .in5(register_6_q), .in6(register_7_q), .in7(register_8_q), .out(out_6), .sel(in_4));
  Multiplexer #(.select(3), .width(32)) multiplexer_2 (
    .in0(register_1_q), .in1(register_2_q), .in2(register_3_q), .in3(register_4_q), .in4(register_5_q),
    .in5(register_6_q), .in6(register_7_q), .in7(register_8_q), .out(out_7), .sel(in_5));
  Decoder #(.select(3)) decoder_1 (
    .out0(decoder_1_out0), .out1(decoder_1_out1), .out2(decoder_1_out2), .out3(decoder_1_out3),
    .out4(decoder_1_out4), .out5(decoder_1_out5), .out6(decoder_1_out6), .out7(decoder_1_out7), .sel(in_3),
    .en(1'b1));
  Register #(.width(32)) register_1 (.D(in_1), .en(and_1_out), .clk(clock_1_out), .Q(register_1_q));  // open: clr
  and and_1 (and_1_out, in_2, decoder_1_out0);
  Register #(.width(32)) register_2 (.D(in_1), .en(and_2_out), .clk(clock_1_out), .Q(register_2_q));  // open: clr
  and and_2 (and_2_out, in_2, decoder_1_out1);
  Register #(.width(32)) register_3 (.D(in_1), .en(and_3_out), .clk(clock_1_out), .Q(register_3_q));  // open: clr
  and and_3 (and_3_out, in_2, decoder_1_out2);
  Register #(.width(32)) register_4 (.D(in_1), .en(and_4_out), .clk(clock_1_out), .Q(register_4_q));  // open: clr
  and and_4 (and_4_out, in_2, decoder_1_out3);
  Register #(.width(32)) register_5 (.D(in_1), .en(and_5_out), .clk(clock_1_out), .Q(register_5_q));  // open: clr
  and and_5 (and_5_out, in_2, decoder_1_out4);
  Register #(.width(32)) register_6 (.D(in_1), .en(and_6_out), .clk(clock_1_out), .Q(register_6_q));  // open: clr
  and and_6 (and_6_out, in_2, decoder_1_out5);
  Register #(.width(32)) register_7 (.D(in_1), .en(and_7_out), .clk(clock_1_out), .Q(register_7_q));  // open: clr
  and and_7 (and_7_out, in_2, decoder_1_out6);
  Register #(.width(32)) register_8 (.D(in_1), .en(and_8_out), .clk(clock_1_out), .Q(register_8_q));  // open: clr
  and and_8 (and_8_out, in_2, decoder_1_out7);

  // Notes on the sheet:
  //   busWrite
  //   WriteEnable
  //   WriteRegNo
  //   ReadA&BusA
  //   ReadB&BusB
endmodule

module exp1310 (
  input  [31:0] in_1,
  input  in_2,
  input  [2:0] in_3,
  input  [2:0] in_4,
  input  [2:0] in_5,
  output [31:0] out_6,
  output [31:0] out_7
);

  Clock clock_1 ();  // open: out
  exp1310_handmade_regfile exp1310_handmade_regfile_1 (
    .in_1(in_1), .in_2(in_2), .in_3(in_3), .in_4(in_4), .in_5(in_5), .out_6(out_6), .out_7(out_7));

  // Notes on the sheet:
  //   busWrite
  //   WriteEnable
  //   WriteRegNo
  //   ReadA&BusA
  //   ReadB&BusB
endmodule
