// Logisim project exp_2.circ as structural Verilog: 8 circuits, main circuit CLA4bit
module CLA4bit (
  input  [3:0] B,
  input  [3:0] A,
  input  Cin,
  output Cout,
  output [3:0] out_5,
  output Gg,
  output Pg
);

  wire and_1_out, and_2_out, and_3_out, and_4_out, and_5_out, and_6_out, and_7_out, and_10_out, and_11_out,
       and_12_out, nand_1_out, nand_2_out, nand_3_out, nand_4_out, nor_1_out, nor_2_out, nor_3_out,
       nor_4_out, not_1_out, not_2_out, not_3_out, not_4_out, not_5_out, not_6_out, not_7_out, or_1_out,
       or_2_out, or_3_out, or_4_out, or_5_out, or_6_out, or_7_out, or_8_out, or_9_out, or_10_out;

  nand nand_1 (nand_1_out, B[3], A[3]);
  nor nor_1 (nor_1_out, B[3], A[3]);
  nand nand_2 (nand_2_out, B[2], A[2]);
  nor nor_2 (nor_2_out, B[2], A[2]);
  nand nand_3 (nand_3_out, B[1], A[1]);
  nor nor_3 (nor_3_out, B[1], A[1]);
  nand nand_4 (nand_4_out, B[0], A[0]);
  nor nor_4 (nor_4_out, B[0], A[0]);
  not not_1 (not_1_out, Cin);
  not not_2 (not_2_out, nor_1_out);
  or or_1 (or_1_out, ~nor_2_out, ~nand_1_out);  // OR_Gate
  or or_2 (or_2_out, ~nor_3_out, ~nand_2_out, ~nand_1_out);  // OR_Gate
  or or_3 (or_3_out, ~nor_4_out, ~nand_3_out, ~nand_2_out, ~nand_1_out);  // OR_Gate
  or or_4 (or_4_out, ~not_1_out, ~nand_4_out, ~nand_3_out, ~nand_2_out, ~nand_1_out);  // OR_Gate
  and and_1 (and_1_out, nand_1_out, ~nor_1_out);  // AND_Gate
  not not_3 (not_3_out, nor_2_out);
  or or_5 (or_5_out, ~nor_3_out, ~nand_2_out);  // OR_Gate
  or or_6 (or_6_out, ~nor_4_out, ~nand_3_out, ~nand_2_out);  // OR_Gate
  or or_7 (or_7_out, ~not_1_out, ~nand_4_out, ~nand_3_out, ~nand_2_out);  // OR_Gate
  and and_2 (and_2_out, nand_2_out, ~nor_2_out);  // AND_Gate
  not not_4 (not_4_out, nor_3_out);
  or or_8 (or_8_out, ~nor_4_out, ~nand_3_out);  // OR_Gate
  or or_9 (or_9_out, ~not_1_out, ~nand_4_out, ~nand_3_out);  // OR_Gate
  and and_3 (and_3_out, nand_3_out, ~nor_3_out);  // AND_Gate
  not not_5 (not_5_out, nor_4_out);
  or or_10 (or_10_out, ~not_1_out, ~nand_4_out);  // OR_Gate
  and and_4 (and_4_out, nand_4_out, ~nor_4_out);  // AND_Gate
  not not_6 (not_6_out, not_1_out);
  not not_7 (not_7_out, nand_1_out);
  and and_5 (and_5_out, ~nand_2_out, ~nor_1_out);  // AND_Gate
  and and_6 (and_6_out, ~nor_2_out, ~nand_3_out, ~nor_1_out);  // AND_Gate
  and and_7 (and_7_out, ~nor_3_out, ~nor_2_out, ~nand_4_out, ~nor_1_out);  // AND_Gate
  and and_8 (Pg, ~nor_4_out, ~nor_3_out, ~nor_2_out, ~nor_1_out);  // AND_Gate
  and and_9 (Cout, not_2_out, or_1_out, or_2_out, or_3_out, or_4_out);
  and and_10 (and_10_out, not_3_out, or_5_out, or_6_out, or_7_out);
  and and_11 (and_11_out, not_4_out, or_8_out, or_9_out);
  and and_12 (and_12_out, not_5_out, or_10_out);
  or or_11 (Gg, not_7_out, and_5_out, and_6_out, and_7_out);
  xor xor_1 (out_5[3], and_1_out, and_10_out);
  xor xor_2 (out_5[2], and_2_out, and_11_out);
  xor xor_3 (out_5[1], and_3_out, and_12_out);
  xor xor_4 (out_5[0], and_4_out, not_6_out);

  // Notes on the sheet:
  //   B3
  //   A3
  //   B2
  //   A2
  //   B1
  //   A1
  //   B0
  //   A0
  //   S3
  //   S2
  //   S1
  //   S0
endmodule

module CLU4bit (
  input  P0,
  input  G0,
  input  P1,
  input  G1,
  input  P2,
  input  G2,
  input  P3,
  input  G3,
  input  C0,
  output C1,
  output C2,
  output C3,
  output C4,
  output GS0,
  output PS0
);

  wire and_1_out, and_2_out, and_3_out, and_4_out, and_5_out, and_6_out, and_7_out, and_8_out, and_9_out,
       and_10_out;

  and and_1 (and_1_out, P0, C0);
  and and_2 (and_2_out, G0, P1);
  and and_3 (and_3_out, P1, P0, C0);
  and and_4 (and_4_out, G1, P2);
  and and_5 (and_5_out, G0, P1, P2);
  and and_6 (and_6_out, P0, C0, P1, P2);
  and and_7 (and_7_out, G2, P3);
  and and_8 (and_8_out, G1, P2, P3);
  and and_9 (and_9_out, G0, P1, P2, P3);
  and and_10 (and_10_out, P0, G0, P1, P2, P3);
  or or_1 (C1, and_1_out, G0);
  or or_2 (C2, and_2_out, and_3_out, G1);
  or or_3 (C3, and_4_out, and_5_out, and_6_out, G2);
  or or_4 (C4, and_7_out, and_8_out, and_9_out, and_10_out, G3);
  or or_5 (GS0, and_7_out, and_8_out, and_9_out, and_9_out);
  or or_6 (PS0, P0, P3, P1, P2);
endmodule

module CLA16bit (
  input  Cin,
  input  [15:0] in_2,
  input  [15:0] in_3,
  output Cout,
  output GS0,
  output PS0,
  output [15:0] out_7
);

  wire cla4bit_1_gg, cla4bit_1_pg, cla4bit_2_gg, cla4bit_2_pg, cla4bit_3_gg, cla4bit_3_pg, cla4bit_4_gg,
       cla4bit_4_pg, clu4bit_1_c1, clu4bit_1_c2, clu4bit_1_c3;

  CLA4bit cla4bit_1 (
    .Cin(Cin), .B(in_3[3:0]), .A(in_2[3:0]), .out_5(out_7[3:0]), .Pg(cla4bit_1_pg), .Gg(cla4bit_1_gg));  // open: Cout
  CLA4bit cla4bit_2 (
    .Cin(clu4bit_1_c1), .B(in_3[7:4]), .A(in_2[7:4]), .out_5(out_7[7:4]), .Pg(cla4bit_2_pg), .Gg(cla4bit_2_gg));  // open: Cout
  CLA4bit cla4bit_3 (
    .Cin(clu4bit_1_c2), .B(in_3[11:8]), .A(in_2[11:8]), .out_5(out_7[11:8]), .Pg(cla4bit_3_pg),
    .Gg(cla4bit_3_gg));  // open: Cout
  CLA4bit cla4bit_4 (
    .Cin(clu4bit_1_c3), .B(in_3[15:12]), .A(in_2[15:12]), .out_5(out_7[15:12]), .Pg(cla4bit_4_pg),
    .Gg(cla4bit_4_gg));  // open: Cout
  CLU4bit clu4bit_1 (
    .P0(cla4bit_1_pg), .G0(cla4bit_1_gg), .P1(cla4bit_2_pg), .G1(cla4bit_2_gg), .P2(cla4bit_3_pg),
    .G2(cla4bit_3_gg), .P3(cla4bit_4_pg), .G3(cla4bit_4_gg), .C0(Cin), .PS0(PS0), .C1(clu4bit_1_c1),
    .C2(clu4bit_1_c2), .C3(clu4bit_1_c3), .C4(Cout), .GS0(GS0));

  // Notes on the sheet:
  //   A
  //   B
  //   0
  //   1
  //   2
  //   3
endmodule

module CLA32bit (
  input  Cin,
  input  [31:0] in_2,
  input  [31:0] in_3,
  output Cout,
  output CF,
  output SF,
  output OF,
  output ZF,
  output [31:0] out_9
);

  wire cla16bit_1_cout;

  CLA16bit cla16bit_1 (
    .in_2(in_2[15:0]), .in_3(in_3[15:0]), .Cin(Cin), .Cout(cla16bit_1_cout), .out_7(out_9[15:0]));  // open: GS0, PS0
  CLA16bit cla16bit_2 (
    .in_2(in_2[31:16]), .in_3(in_3[31:16]), .Cin(cla16bit_1_cout), .Cout(Cout), .out_7(out_9[31:16]));  // open: GS0, PS0
  nor nor_1 (ZF, out_9[0], out_9[1], out_9[2], out_9[3], out_9[4], out_9[5], out_9[6], out_9[7], out_9[8], out_9[9], out_9[10], out_9[11], out_9[12], out_9[13], out_9[14], out_9[15], out_9[16], out_9[17], out_9[18], out_9[19], out_9[20], out_9[21], out_9[22], out_9[23], out_9[24], out_9[25], out_9[26], out_9[27], out_9[28], out_9[29], out_9[30], out_9[31]);
  xor xor_1 (CF, Cout, Cin);
  xor xor_2 (OF, Cout, cla16bit_1_cout);

  assign SF = out_9[31];

  // Notes on the sheet:
  //   A
  //   B
endmodule

module ALUControl (
  input  [3:0] in_1,
  output [1:0] OPcontrol,
  output Sigcontrol,
  output SUBconrtol
);

  wire and_1_out, and_2_out, and_3_out, and_4_out, and_5_out;

  and and_1 (and_1_out, ~in_1[0], ~in_1[3], in_1[1], in_1[2]);  // AND_Gate
  and and_2 (and_2_out, in_1[1], ~in_1[2], ~in_1[3]);  // AND_Gate
  and and_3 (and_3_out, in_1[0], in_1[1], in_1[2], in_1[3]);
  and and_4 (and_4_out, in_1[1], ~in_1[2], ~in_1[3]);  // AND_Gate
  not not_1 (Sigcontrol, in_1[0]);
  and and_5 (and_5_out, in_1[1], ~in_1[2], ~in_1[3]);  // AND_Gate
  or or_1 (OPcontrol[0], and_1_out, and_2_out);
  or or_2 (OPcontrol[1], and_3_out, and_4_out);
  or or_3 (SUBconrtol, and_5_out, in_1[3]);
endmodule

module ALU (
  input  [31:0] in_1,
  input  [31:0] in_2,
  input  [3:0] in_3,
  output [1:0] OPctr,
  output [31:0] out_5,
  output ZF,
  output CF,
  output SF,
  output OF
);

  wire alucontrol_1_sigcontrol, alucontrol_1_subconrtol, multiplexer_1_out, xor_2_out;
  wire [31:0] bit_extender_1_out, bit_extender_2_out, cla32bit_1_out_9, or_1_out, xor_1_out;

  ALUControl alucontrol_1 (
    .in_1(in_3), .OPcontrol(OPctr), .Sigcontrol(alucontrol_1_sigcontrol), .SUBconrtol(alucontrol_1_subconrtol));
  assign bit_extender_1_out = {{31{alucontrol_1_subconrtol}}, alucontrol_1_subconrtol};  // Bit_Extender bit_extender_1
  assign or_1_out = in_2 | in_1;  // OR_Gate or_1, 32 bits wide
  CLA32bit cla32bit_1 (
    .Cin(alucontrol_1_subconrtol), .in_2(in_1), .in_3(xor_1_out), .CF(CF), .SF(SF), .OF(OF), .ZF(ZF),
    .out_9(cla32bit_1_out_9));  // open: Cout
  assign xor_1_out = in_2 ^ bit_extender_1_out;  // XOR_Gate xor_1, 32 bits wide
  xor xor_2 (xor_2_out, OF, SF);
  assign bit_extender_2_out = {{31{1'b0}}, multiplexer_1_out};  // Bit_Extender bit_extender_2
  Multiplexer multiplexer_1 (.in0(CF), .in1(xor_2_out), .out(multiplexer_1_out), .sel(alucontrol_1_sigcontrol));
  Multiplexer #(.select(2), .width(32)) multiplexer_2 (
    .in0(cla32bit_1_out_9), .in1(or_1_out), .in2(in_2), .in3(bit_extender_2_out), .out(out_5), .sel(OPctr));

  // Notes on the sheet:
  //   A
  //   B
  //   ALUControl
  //   Result
endmodule

module exp_2_2_1 (
  input  [11:0] in_1,
  input  [31:0] in_2,
  input  WE,
  input  RE,
  output [31:0] out_5
);

  wire button_1_out, clock_1_out;

  RAM #(.addrWidth(12), .clearpin("true"), .dataWidth(32), .enables("line")) ram_1 (
    .addr(in_1), .we(WE), .clk(clock_1_out), .din(in_2), .dout(out_5), .clr(button_1_out));
  Clock clock_1 (.out(clock_1_out));
  Button button_1 (.out(button_1_out));

  // Notes on the sheet:
  //   Clear
endmodule

module exp_2_2_2 (
  input  [11:0] in_1,
  input  [7:0] in_2,
  input  WE,
  input  RE
);

  wire button_1_out, button_2_out, clock_1_out;
  wire [7:0] ram_1_dout;

  Clock clock_1 (.out(clock_1_out));
  Button button_1 (.out(button_1_out));
  RAM #(.addrWidth(12), .clearpin("true"), .enables("line")) ram_1 (
    .addr(in_1), .we(WE), .clk(clock_1_out), .din(in_2), .dout(ram_1_dout), .clr(button_1_out));
  TTY tty_1 (.data(ram_1_dout[6:0]), .clk(clock_1_out), .we(RE), .clr(button_2_out));
  Button button_2 (.out(button_2_out));

  // Notes on the sheet:
  //   Clear
  //   Clear
endmodule
