// Logisim project exp_4.circ as structural Verilog: 3 circuits, main circuit ImmTolmm
module ImmTolmm (
  input  [31:0] in_1,
  input  [2:0] in_2,
  output [31:0] out_3
);

  wire [11:0] bit_extender_4_out;
  wire [19:0] bit_extender_1_out, bit_extender_2_out, bit_extender_3_out;

  assign bit_extender_1_out = {{19{in_1[31]}}, in_1[31]};  // Bit_Extender bit_extender_1
  assign bit_extender_2_out = {{19{in_1[31]}}, in_1[31]};  // Bit_Extender bit_extender_2
  assign bit_extender_3_out = {{19{in_1[31]}}, in_1[31]};  // Bit_Extender bit_extender_3
  assign bit_extender_4_out = {{11{in_1[31]}}, in_1[31]};  // Bit_Extender bit_extender_4
  Multiplexer #(.select(3), .width(32)) multiplexer_1 (
    .in0({bit_extender_1_out, in_1[31:20]}), .in1({in_1[31:12], {12{1'b0}}}),
    .in2({bit_extender_2_out, in_1[31:25], in_1[11:7]}),
    .in3({bit_extender_3_out, in_1[7], in_1[30:25], in_1[11:8], 1'b0}),
    .in4({bit_extender_4_out, in_1[19:12], in_1[20], in_1[30:21], 1'b0}), .in5({32{1'b0}}), .in6({32{1'b0}}),
    .in7({32{1'b0}}), .out(out_3), .sel(in_2));

  // Notes on the sheet:
  //   Instr
  //   ExtOp
  //   I
  //   U
  //   S
  //   B
  //   J
  //   imm
endmodule

module CmdDecoder (
  input  [31:0] in_1,
  input  [2:0] ExtOp,
  output [6:0] out_3,
  output [4:0] out_4,
  output [2:0] out_5,
  output [4:0] out_6,
  output [4:0] out_7,
  output [6:0] out_8,
  output [31:0] out_9
);

  ImmTolmm immtolmm_1 (.in_1(in_1), .in_2(ExtOp), .out_3(out_9));
  // Probe on out_9

  assign out_3 = in_1[6:0];
  assign out_4 = in_1[11:7];
  assign out_5 = in_1[14:12];
  assign out_6 = in_1[19:15];
  assign out_7 = in_1[24:20];
  assign out_8 = in_1[31:25];

  // Notes on the sheet:
  //   InStr
  //   Rd
  //   Rs1
  //   Rs2
  //   OpCode
  //   Funct3
  //   Funct7
  //   Imm
endmodule

module main (
  input  Branch,
  input  Zero,
  input  Jump,
  input  [2:0] ExtOp,
  output [31:0] out_5,
  output [31:0] out_6,
  output [6:0] out_7,
  output [4:0] out_8,
  output [2:0] out_9,
  output [4:0] out_10,
  output [4:0] out_11,
  output [6:0] out_12
);

  wire and_1_out, button_1_out, clock_1_out, or_1_out;
  wire [31:0] adder_1_out, multiplexer_1_out, register_1_q;

  Clock clock_1 (.out(clock_1_out));
  Button button_1 (.out(button_1_out));
  and and_1 (and_1_out, Zero, Branch);
  CmdDecoder cmddecoder_1 (
    .in_1(out_6), .ExtOp(ExtOp), .out_9(out_5), .out_3(out_7), .out_4(out_8), .out_5(out_9), .out_6(out_10),
    .out_7(out_11), .out_8(out_12));
  Register #(.width(32)) register_1 (
    .D(adder_1_out), .clk(clock_1_out), .Q(register_1_q), .clr(button_1_out));  // open: en
  Multiplexer #(.width(32)) multiplexer_1 (.in0(32'h4), .in1(out_5), .out(multiplexer_1_out), .sel(or_1_out));
  or or_1 (or_1_out, Jump, and_1_out);
  Adder #(.width(32)) adder_1 (.a(register_1_q), .b(multiplexer_1_out), .out(adder_1_out));  // open: cin, cout
  // Probe on multiplexer_1_out
  RAM #(.addrWidth(12), .dataWidth(32), .enables("line")) ram_1 (
    .addr(register_1_q[13:2]), .clk(clock_1_out), .dout(out_6));  // open: we, din

  // Notes on the sheet:
  //   Reset
  //   Imm
  //   Instr
  //   OpCode
  //   Rd
  //   Funct3
  //   Rs1
  //   Rs2
  //   Funct7
endmodule
